# Fritzing sketch arduino_8253 (saved by Fritzing 0.9.10b)
breadboards: 1

parts:
  Part1 = Arduino Uno (Rev3)
  IC1 = IC, DIP package, 22 pins [chip_label=i8253]
  IC1_2 = IC, DIP package, 24 pins [chip_label=i8253]
  Q1 = NPN-Transistor [package="TO92 [THT]"]
  R1 = Resistor [tolerance=±5% power=0.25 resistance=1000 package=THT]
  LED1 = smd LED [color="Blue (505nm)" current=0.030 package="0603 [SMD]"]
  LED2 = smd LED [color="Blue (505nm)" current=0.030 package="0603 [SMD]"]
  LED3 = smd LED [color="Blue (505nm)" current=0.030 package="0603 [SMD]"]
  R2 = Resistor [tolerance=±5% power=0.25 resistance=470 package=THT]
  R3 = Resistor [tolerance=±5% power=0.25 resistance=470 package=THT]
  R4 = Resistor [tolerance=±5% power=0.25 resistance=470 package=THT]
  LED4 = LED - 5mm [color="White (6500K)" current=0.030 package="5 mm [THT]"]
  LED5 = LED - 5mm [color="White (6500K)" current=0.030 package="5 mm [THT]"]
  LED6 = LED - 5mm [color="White (6500K)" current=0.030 package="5 mm [THT]"]
  LED7 = LED - 5mm [color="White (6500K)" current=0.030 package="5 mm [THT]"]
  LED8 = LED - 5mm [color="White (6500K)" current=0.030 package="5 mm [THT]"]
  LED9 = LED - 5mm [color="White (6500K)" current=0.030 package="5 mm [THT]"]
  LED10 = LED - 5mm [color="White (6500K)" current=0.030 package="5 mm [THT]"]
  LED11 = LED - 5mm [color="White (6500K)" current=0.030 package="5 mm [THT]"]
  IC2 = IC, DIP package, 20 pins [chip_label=74LS373]
  U1 = 74HC04_HEX_INVERTER [package=dil14]
  R5 = Resistor [tolerance=±5% power=0.25 resistance=470 package=THT]
  R6 = Resistor [tolerance=±5% power=0.25 resistance=470 package=THT]
  R7 = Resistor [tolerance=±5% power=0.25 resistance=470 package=THT]
  R8 = Resistor [tolerance=±5% power=0.25 resistance=470 package=THT]
  R9 = Resistor [tolerance=±5% power=0.25 resistance=470 package=THT]
  R10 = Resistor [tolerance=±5% power=0.25 resistance=470 package=THT]
  R11 = Resistor [tolerance=±5% power=0.25 resistance=470 package=THT]
  R12 = Resistor [tolerance=±5% power=0.25 resistance=470 package=THT]

nets:
  N1: Part1.A0, IC1.pin10, IC1_2.pin10, LED1.anode
  N2: Part1.A1, IC1_2.pin13, LED2.anode
  N3: Part1.A2, IC1_2.pin17, LED3.anode
  N4: Part1.A3, IC1_2.pin22, U1.1A
  N5: Part1.A4/SDA, IC1_2.pin23
  N6: Part1.A5/SCL, R1.Pin_0
  N7: Part1.D8, IC1.pin8, IC1_2.pin8, IC2.pin3
  N8: Part1.D9_PWM, IC1.pin7, IC1_2.pin7, IC2.pin4
  N9: Part1.D10_PWM/SS, IC1_2.pin19
  N10: Part1.D11_PWM/MOSI, IC1_2.pin20
  N11: Part1.D12/MISO, IC1_2.pin16
  N12: Part1.D13/SCK, IC1.pin9, IC1_2.pin9, IC1_2.pin15, IC1_2.pin18
  GND: Part1.GND, IC1_2.pin12, IC1_2.pin21, R2.Pin_0, R3.Pin_0, R4.Pin_0, IC2.pin10, U1.GND, R5.Pin_0, R6.Pin_0, R7.Pin_0, R8.Pin_0, R9.Pin_0, R10.Pin_0, R11.Pin_0, R12.Pin_0
  N13: Part1.D2, IC1.pin6, IC1_2.pin6, IC2.pin7
  N14: Part1.D3_PWM, IC1.pin5, IC1_2.pin5, IC2.pin8
  N15: Part1.D4, IC1.pin4, IC1_2.pin4, IC2.pin13
  N16: Part1.D5_PWM, IC1.pin3, IC1_2.pin3, IC2.pin14
  N17: Part1.D6_PWM, IC1.pin2, IC1_2.pin2, IC2.pin17
  N18: Part1.D7, IC1.pin1, IC1_2.pin1, IC2.pin18
  5V: Part1.5V, IC1.pin11, IC1_2.pin11, IC1_2.pin14, IC1_2.pin24, Q1.E, Q1.C, LED4.anode, IC2.pin19, U1.VCC
  N19: Q1.B, R1.Pin_1
  N20: LED1.cathode, R4.Pin_1
  N21: LED2.cathode, R3.Pin_1
  N22: LED3.cathode, R2.Pin_1
  N23: LED4.cathode, R12.Pin_1
  N24: LED5.cathode, R11.Pin_1
  N25: LED5.anode, IC2.pin16
  N26: LED6.cathode, R10.Pin_1
  N27: LED6.anode, IC2.pin15
  N28: LED7.cathode, R9.Pin_1
  N29: LED7.anode, IC2.pin12
  N30: LED8.cathode, R8.Pin_1
  N31: LED8.anode, IC2.pin9
  N32: LED9.cathode, R7.Pin_1
  N33: LED9.anode, IC2.pin6
  N34: LED10.cathode, R6.Pin_1
  N35: LED10.anode, IC2.pin5
  N36: LED11.cathode, R5.Pin_1
  N37: LED11.anode, IC2.pin2
  N38: IC2.pin1, IC2.pin11, U1.1Y
